// Logisim project ex3.circ as structural Verilog: 1 circuit, main circuit AddMachine
module AddMachine (
  input  clk,
  output [7:0] ADD_OUT,
  output [7:0] REG_OUT
);

  Adder adder_1 (.a(REG_OUT), .b(8'h1), .out(ADD_OUT));  // open: cin, cout
  Register register_1 (.D(ADD_OUT), .clk(clk), .Q(REG_OUT));  // open: en, clr

  // Notes on the sheet:
  //   Q(t+1)=D(t)
  //   reg updates as clk
endmodule
